# Fritzing sketch ornament (saved by Fritzing 0.8.5b)
breadboards: 1

parts:
  LED1 = RGB LED - (4 legs) [package="5 mm [THT]"]
  R1 = Resistor [tolerance=±5% resistance=330 package=THT]
  R2 = Resistor [tolerance=±5% resistance=330 package=THT]
  R3 = Resistor [tolerance=±5% resistance=330 package=THT]
  Part1 = Arduino Uno (Rev3)

nets:
  N1: LED1.red_cathode, R1.Pin_0
  N2: LED1.common_anode, Part1.5V
  N3: LED1.green_cathode, R2.Pin_0
  N4: LED1.blue_cathode, R3.Pin_0
  N5: R1.Pin_1, Part1.D11_PWM/MOSI
  N6: R2.Pin_1, Part1.D10_PWM/SS
  N7: R3.Pin_1, Part1.D9_PWM
